# Fritzing sketch p2_esq (saved by Fritzing 0.9.6b)
breadboards: 1

parts:
  LCD1 = LCD screen
  LED1 = LED - 5mm [color="Red (633nm)" current=0.030 package="5 mm [THT]"]
  LED2 = LED - 5mm [color="Green (570nm)" current=0.030 package="5 mm [THT]"]
  Part1 = Arduino Uno (Rev3)
  R2 = Resistor [tolerance=±5% power=0.25 resistance=1000 package=THT]
  R1 = Resistor [tolerance=±5% power=0.25 resistance=1000 package=THT]
  R3 = Trimmer Potentiometer [maximum_resistance=10kΩ package=THT]
  R4 = Resistor [tolerance=±5% power=0.25 resistance=1000 package=THT]
  Part2 = Thumb Joystick
  HC-SR04_Sensor_1 = HC-SR04 Ultrasonic Distance Sensor
  S1 = Pushbutton [package="[THT]"]
  RHT1 = Humidity and Temperature Sensor RHT03

nets:
  GND: LCD1.VSS, LCD1.R/W, LCD1.LED-, LED1.cathode, LED2.cathode, Part1.GND, R3.leg1, Part2.GND, HC-SR04_Sensor_1.GND, S1.Pin_1, S1.Pin_2, RHT1.GND_1
  VCC: LCD1.VDD, Part1.5V, R3.leg2, R4.Pin_1, Part2.VCC, HC-SR04_Sensor_1.VCC, RHT1.Data-signal
  N1: LCD1.V0, R3.wiper
  N2: LCD1.RS, Part1.D11_PWM/MOSI
  N3: LCD1.E, Part1.D10_PWM/SS
  N4: LCD1.DB4, Part1.D9_PWM
  N5: LCD1.DB5, Part1.D8
  N6: LCD1.DB6, Part1.D7
  N7: LCD1.DB7, Part1.D6_PWM
  N8: LCD1.LED+, R4.Pin_0
  N9: LED1.anode, R1.Pin_0
  N10: LED2.anode, R2.Pin_0
  N11: Part1.A0, Part2.HORZ
  N12: Part1.A1, Part2.VERT
  N13: Part1.A5/SCL, R1.Pin_1
  N14: Part1.D12/MISO, HC-SR04_Sensor_1.TRIG
  N15: Part1.D13/SCK, HC-SR04_Sensor_1.ECHO
  N16: Part1.D2, S1.Pin_3, S1.Pin_4
  N17: Part1.D3_PWM, R2.Pin_1
  N18: Part1.D4, Part2.SEL
  N19: Part1.D5_PWM, RHT1.Vcc
